# Fritzing sketch imx6ul_schematics (saved by Fritzing 0.9.3b)

parts:
  Squix1 = OLED 0.96" 128x64 I2C SSD1306
  PICO-PI-IMX6UL = Raspberry Pi 3 [part_number=RPI-3-V1.2]
  BUTTON_PLAY_PAUSE = Pushbutton [package="[THT]"]  # not connected
  BUTTON_VOLUME_UP = Pushbutton [package="[THT]"]  # not connected
  BUTTON_VOLUME_DOWN = Pushbutton [package="[THT]"]  # not connected
  BUTTON_PRESET1 = Pushbutton [package="[THT]"]  # not connected
  BUTTON_PRESET2 = Pushbutton [package="[THT]"]  # not connected

nets:
  VCC: Squix1.VCC, PICO-PI-IMX6UL.5V
  GND: Squix1.GND, PICO-PI-IMX6UL.GND
  N1: Squix1.SCL, PICO-PI-IMX6UL.GPIO3
  N2: Squix1.SCA, PICO-PI-IMX6UL.GPIO2
